# Fritzing sketch Force_finger_schematic (saved by Fritzing 0.9.4)
breadboards: 1

parts:
  Part1 = Arduino Uno (Rev3)
  R1 = Resistor [tolerance=±5% resistance=220 package="2512 [SMD]"]
  R2 = Rotary Potentiometer (Small) [maximum_resistance=100kΩ package=THT]
  J1 = Basic Force Sensing Resistor (FSR) [package=THT]

nets:
  N1: Part1.A0, R1.Pin_1, J1.pin_0
  N2: Part1.A1, R2.wiper
  N3: Part1.5V, R2.leg1, J1.pin_1
  N4: Part1.GND, R1.Pin_0, R2.leg2

notes:
  Partslist:
  - 10kOhm resistor
  - Ohmite FSR07CE FSR
  - Sparkfun U103 390e potmeter
  - Arduino Uno
